// Logisim project BAMF Datapath.circ as structural Verilog: 7 circuits, main circuit main
// memory
module main (
);

  wire ALU_skip, and_1_out;
  wire [2:0] ALU_cmp_out;
  wire [15:0] adder_1_out, adder_2_out, ALU_result, bit_extender_1_out, bit_extender_2_out,
       bit_extender_3_out, bit_extender_4_out, memory_douta, memory_doutb, multiplexer_1_out,
       multiplexer_2_out, multiplexer_3_out, multiplexer_4_out, multiplexer_5_out, multiplexer_6_out,
       multiplexer_7_out, multiplexer_8_out, multiplexer_9_out, PC_pc, registers_flag_out, registers_r_out,
       registers_ra_out, registers_sp_out, shifter_1_out;

  Multiplexer #(.select(2), .width(16), .enable("false")) multiplexer_1 (
    .in0(bit_extender_1_out), .in1(registers_sp_out), .in2(ALU_result), .out(multiplexer_1_out));  // open: in3, sel
  Multiplexer #(.width(16), .enable("false")) multiplexer_2 (
    .in0(ALU_result), .in1(registers_r_out), .out(multiplexer_2_out));  // open: sel
  PC PC (.newpc(multiplexer_5_out), .pc(PC_pc));
  Adder #(.width(16)) adder_1 (.a(16'h2), .b(PC_pc), .out(adder_1_out));  // open: cin, cout
  dual_memory memory (
    .addra(PC_pc), .addrb(multiplexer_1_out), .dinb(multiplexer_2_out), .douta(memory_douta),
    .doutb(memory_doutb));  // open: dina, web, wea
  control control (.instr(memory_douta));
  Multiplexer #(.width(16), .enable("false")) multiplexer_3 (
    .in0(ALU_result), .in1(memory_doutb), .out(multiplexer_3_out));  // open: sel
  Multiplexer #(.width(16), .enable("false")) multiplexer_4 (
    .in0(multiplexer_5_out), .in1(memory_doutb), .out(multiplexer_4_out));  // open: sel
  assign bit_extender_1_out = {{4{1'b0}}, memory_douta[11:0]};  // Bit_Extender bit_extender_1
  assign bit_extender_2_out = {{4{memory_douta[11]}}, memory_douta[11:0]};  // Bit_Extender bit_extender_2
  assign bit_extender_3_out = {{8{1'b0}}, memory_douta[7:0]};  // Bit_Extender bit_extender_3
  assign bit_extender_4_out = {{8{memory_douta[7]}}, memory_douta[7:0]};  // Bit_Extender bit_extender_4
  Multiplexer #(.width(16), .enable("false")) multiplexer_5 (
    .in0(multiplexer_6_out), .in1(adder_2_out), .out(multiplexer_5_out), .sel(and_1_out));
  Multiplexer #(.width(16), .enable("false")) multiplexer_6 (
    .in0(adder_1_out), .in1(ALU_result), .out(multiplexer_6_out));  // open: sel
  registers registers (
    .r_in(multiplexer_3_out), .p_in(ALU_result), .sp_in(ALU_result), .cmp_in(ALU_cmp_out),
    .ra_in(multiplexer_4_out), .r_out(registers_r_out), .flag_out(registers_flag_out),
    .sp_out(registers_sp_out), .ra_out(registers_ra_out));  // open: r_write, r_backup, r_restore, page_write, cmp_write, sp_write, ra_write
  Adder #(.width(16)) adder_2 (.a(16'h2), .b(multiplexer_6_out), .out(adder_2_out));  // open: cin, cout
  Multiplexer #(.select(3), .width(16), .enable("false")) multiplexer_7 (
    .in0(registers_r_out), .in1(registers_flag_out), .in2(registers_sp_out), .in3(registers_ra_out),
    .in4(multiplexer_5_out), .in5({16{1'b0}}), .out(multiplexer_7_out));  // open: in6, in7, sel
  Multiplexer #(.select(4), .width(16), .enable("false")) multiplexer_8 (
    .in0(registers_r_out), .in1(registers_flag_out), .in2(registers_sp_out), .in3(registers_ra_out),
    .in4(bit_extender_1_out), .in5(bit_extender_2_out), .in6(bit_extender_3_out), .in7(bit_extender_4_out),
    .in8(multiplexer_5_out), .in9(16'h1), .in10({16{1'b0}}), .in11({16{1'b1}}), .in12(memory_doutb),
    .out(multiplexer_8_out));  // open: in13, in14, in15, sel
  Shifter #(.width(16)) shifter_1 (.in(multiplexer_8_out), .\dist (4'b0001), .out(shifter_1_out));
  Multiplexer #(.width(16), .enable("false")) multiplexer_9 (
    .in0(shifter_1_out), .in1(multiplexer_8_out), .out(multiplexer_9_out));  // open: sel
  buf and_1 (and_1_out, ALU_skip);  // AND_Gate
  alu ALU (
    .A(multiplexer_7_out), .B(multiplexer_9_out), .cmp_out(ALU_cmp_out), .skip(ALU_skip), .result(ALU_result));  // open: op

  // Notes on the sheet:
  //   memory_addr_src
  //   memory_save_src
  //   instruction
  //   r_src
  //   ra_src
  //   should_jump
  //   ALU_src_A
  //   ALU_src_B
  //   mem_shift
  //   can_skip
  //   should_skip (from ALU)
endmodule

module PC (
  input  [15:0] newpc,
  output [15:0] pc
);


  assign pc = newpc;
endmodule

module memory (
  input  [15:0] addr,
  input  [15:0] data,
  input  write,
  output [15:0] out
);
endmodule

module control (
  input  [15:0] instr
);
endmodule

module registers (
  input  [15:0] r_in,
  input  [15:0] p_in,
  input  [15:0] sp_in,
  input  [2:0] cmp_in,
  input  [15:0] ra_in,
  input  r_write,
  input  r_backup,
  input  r_restore,
  input  page_write,
  input  cmp_write,
  input  sp_write,
  input  ra_write,
  output [15:0] r_out,
  output [15:0] flag_out,
  output [15:0] sp_out,
  output [15:0] ra_out
);
endmodule

module alu (
  input  [15:0] A,
  input  [15:0] B,
  input  [7:0] op,
  output [2:0] cmp_out,
  output skip,
  output [15:0] result
);
endmodule

module dual_memory (
  input  [15:0] addra,
  input  [15:0] dina,
  input  wea,
  input  [15:0] addrb,
  input  [15:0] dinb,
  input  web,
  output [15:0] douta,
  output [15:0] doutb
);
endmodule
